# Fritzing sketch GJK-Watering (saved by Fritzing 0.9.2b)
breadboards: 1

parts:
  Součástka1 = Arduino Uno (Rev3)
  S1 = Pushbutton [package="[THT]"]
  R1 = Resistor [tolerance=±5% resistance=220 package=THT]

nets:
  N1: Součástka1.D8, S1.Pin_1, S1.Pin_2, R1.Pin_0
  N2: Součástka1.5V, S1.Pin_3, S1.Pin_4
  N3: Součástka1.GND, R1.Pin_1

notes:
  Tohle tlačítko spustí nebo vypne zavlažování manuálně
  Tohleto bude vypínat a zapínat tu vodu

// code stored in the sketch: Zavla┼╛ov├ín├¡.ino
// Tahle prom?nná ?íká, zda je zapnuté zavla?ování
int watering_on = 0;

void setup() {
    // N?jakej setup kód
}

void loop() {
    // Tohleto furt dokola
    if (digitalRead(8) == HIGH) {
        // Tla?ítko je zmá?knuto
        if (watering_on) {
            // Vypnout zavla?ování
             watering_on = 0;
        }
        else if (watering_on == 0) {
             // Zapnout zavla?ování
             watering_on = 1;
        }
    }
}
